// Logisim project alu.circ as structural Verilog: 1 circuit, main circuit alu
module alu (
  input  [31:0] A,
  input  [31:0] B,
  input  [3:0] ALUSel,
  output [31:0] Result
);

  wire adder_5_cout, comparator_1_lt, comparator_2_lt, comparator_3_lt, xor_2_out;
  wire [31:0] add0, adder_2_out, adder_3_out, adder_4_out, and1, bit_extender_1_out, bsel13, divu8, mul10,
       mulh14, mulhu11, multiplexer_4_out, multiplexer_5_out, multiplier_3_cout, multiplier_3_out, not_1_out,
       not_2_out, not_3_out, not_4_out, or2, remu9, sll6, slt7, sra5, srl4, sub12, xor3;

  Comparator #(.width(32)) comparator_1 (.a(A), .b(B), .lt(comparator_1_lt));  // open: gt, eq
  Divider #(.width(32)) divider_1 (.a(A), .b(B), .out(divu8));  // open: upper, rem
  Divider #(.width(32)) divider_2 (.a(A), .b(B), .rem(remu9));  // open: out, upper
  Multiplier #(.width(32)) multiplier_1 (.a(A), .b(B), .out(mul10));  // open: cin, cout
  Adder #(.width(32)) adder_1 (.a(A), .b(B), .out(add0));  // open: cin, cout
  assign and1 = A & B;  // AND_Gate and_1, 32 bits wide
  assign or2 = A | B;  // OR_Gate or_1, 32 bits wide
  assign xor3 = A ^ B;  // XOR_Gate xor_1, 32 bits wide
  Shifter #(.width(32), .shift("lr")) shifter_1 (.in(A), .\dist (B[4:0]), .out(srl4));
  Shifter #(.width(32), .shift("ar")) shifter_2 (.in(A), .\dist (B[4:0]), .out(sra5));
  Shifter #(.width(32)) shifter_3 (.in(A), .\dist (B[4:0]), .out(sll6));
  Multiplexer #(.width(32), .enable("false")) multiplexer_1 (
    .in0({32{1'b0}}), .in1(32'h1), .out(slt7), .sel(comparator_1_lt));
  Multiplier #(.width(32)) multiplier_2 (.a(A), .b(B), .cout(mulhu11));  // open: out, cin
  Subtractor #(.width(32)) subtractor_1 (.a(A), .b(B), .out(sub12));  // open: bin, bout
  Multiplexer #(.width(32), .enable("false")) multiplexer_2 (.in0(A), .in1(B), .out(bsel13), .sel(1'b1));
  Multiplexer #(.select(4), .width(32)) multiplexer_3 (
    .in0(add0), .in1(and1), .in2(or2), .in3(xor3), .in4(srl4), .in5(sra5), .in6(sll6), .in7(slt7),
    .in8(divu8), .in9(remu9), .in10(mul10), .in11(mulhu11), .in12(sub12), .in13(bsel13), .in14(mulh14),
    .out(Result), .sel(ALUSel));  // open: in15, en
  Comparator #(.width(32)) comparator_2 (.a(A), .b({32{1'b0}}), .lt(comparator_2_lt));  // open: gt, eq
  Comparator #(.width(32)) comparator_3 (.a(B), .b({32{1'b0}}), .lt(comparator_3_lt));  // open: gt, eq
  assign not_1_out = ~A;  // NOT_Gate not_1, 32 bits wide
  assign not_2_out = ~B;  // NOT_Gate not_2, 32 bits wide
  Multiplexer #(.width(32), .enable("false")) multiplexer_4 (
    .in0(A), .in1(adder_2_out), .out(multiplexer_4_out), .sel(comparator_2_lt));
  Adder #(.width(32)) adder_2 (.a(not_1_out), .b(32'h1), .out(adder_2_out));  // open: cin, cout
  Multiplexer #(.width(32), .enable("false")) multiplexer_5 (
    .in0(B), .in1(adder_3_out), .out(multiplexer_5_out), .sel(comparator_3_lt));
  Adder #(.width(32)) adder_3 (.a(not_2_out), .b(32'h1), .out(adder_3_out));  // open: cin, cout
  Multiplier #(.width(32)) multiplier_3 (
    .a(multiplexer_4_out), .b(multiplexer_5_out), .out(multiplier_3_out), .cout(multiplier_3_cout));  // open: cin
  xor xor_2 (xor_2_out, comparator_2_lt, comparator_3_lt);
  assign not_3_out = ~multiplier_3_out;  // NOT_Gate not_3, 32 bits wide
  assign not_4_out = ~multiplier_3_cout;  // NOT_Gate not_4, 32 bits wide
  Adder #(.width(32)) adder_4 (.a(not_4_out), .b(bit_extender_1_out), .out(adder_4_out));  // open: cin, cout
  Adder #(.width(32)) adder_5 (.a(not_3_out), .b(32'h1), .cout(adder_5_cout));  // open: out, cin
  Multiplexer #(.width(32), .enable("false")) multiplexer_6 (
    .in0(multiplier_3_cout), .in1(adder_4_out), .out(mulh14), .sel(xor_2_out));
  assign bit_extender_1_out = {{31{adder_5_cout}}, adder_5_cout};  // Bit_Extender bit_extender_1

  // Notes on the sheet:
  //   INPUTS to your circuit
  //   DON'T CHANGE THE LOCATIONS OF THE INPUTS AND OUTPUTS!
  //   OUTPUT from your circuit
endmodule
