// Logisim project control_logic.circ as structural Verilog: 6 circuits, main circuit control_logic
module control_logic (
  input  [31:0] inst,
  input  BrEq,
  input  BrLt,
  output PCSel,
  output RegWEn,
  output [2:0] ImmSel,
  output BrUn,
  output ASel,
  output BSel,
  output [3:0] ALUSel,
  output MemRW,
  output [1:0] WBSel
);

  wire and_1_out, and_2_out, and_3_out, and_4_out, and_5_out, and_7_out, and_8_out, and_9_out, and_10_out,
       and_11_out, and_12_out, and_13_out, and_14_out, and_15_out, and_16_out, and_17_out, and_18_out,
       and_19_out, and_20_out, and_21_out, and_22_out, and_23_out, and_24_out, and_26_out, and_27_out,
       and_28_out, comparator_1_eq, comparator_2_eq, comparator_3_eq, comparator_4_eq, comparator_5_eq,
       comparator_6_eq, comparator_7_eq, comparator_8_eq, comparator_9_eq, comparator_10_eq,
       comparator_11_eq, comparator_12_eq, comparator_13_eq, comparator_14_eq, comparator_15_eq,
       comparator_16_eq, comparator_17_eq, comparator_18_eq, comparator_19_eq, comparator_20_eq,
       comparator_21_eq, comparator_22_eq, comparator_23_eq, comparator_24_eq, comparator_25_eq,
       comparator_26_eq, comparator_27_eq, comparator_28_eq, comparator_29_eq, comparator_31_eq,
       comparator_32_eq, comparator_33_eq, comparator_34_eq, comparator_35_eq, comparator_36_eq,
       comparator_37_eq, comparator_38_eq, comparator_39_eq, comparator_40_eq, comparator_41_eq,
       comparator_42_eq, comparator_43_eq, comparator_44_eq, comparator_45_eq, comparator_46_eq,
       comparator_47_eq, comparator_48_eq, comparator_49_eq, comparator_50_eq, comparator_51_eq,
       comparator_52_eq, comparator_53_eq, comparator_54_eq, comparator_55_eq, comparator_56_eq,
       comparator_57_eq, comparator_58_eq, comparator_59_eq, comparator_60_eq, comparator_61_eq,
       comparator_62_eq, comparator_63_eq, or_2_out, or_5_out;

  Comparator #(.width(7)) comparator_1 (.a(inst[6:0]), .b(7'b1100111), .eq(comparator_1_eq));  // open: gt, lt
  Comparator #(.width(3)) comparator_2 (.a(inst[14:12]), .b(3'b110), .eq(comparator_2_eq));  // open: gt, lt
  Comparator #(.width(3)) comparator_3 (.a(inst[14:12]), .b(3'b000), .eq(comparator_3_eq));  // open: gt, lt
  Comparator #(.width(7)) comparator_4 (.a(inst[6:0]), .b(7'b1100011), .eq(comparator_4_eq));  // open: gt, lt
  and and_1 (and_1_out, comparator_4_eq, comparator_5_eq, BrEq);
  Comparator #(.width(3)) comparator_5 (.a(inst[14:12]), .b(3'b000), .eq(comparator_5_eq));  // open: gt, lt
  Comparator #(.width(7)) comparator_6 (.a(inst[6:0]), .b(7'b1100011), .eq(comparator_6_eq));  // open: gt, lt
  and and_2 (and_2_out, comparator_6_eq, comparator_7_eq, BrLt);
  Comparator #(.width(3)) comparator_7 (.a(inst[14:12]), .b(3'b100), .eq(comparator_7_eq));  // open: gt, lt
  Comparator #(.width(7)) comparator_8 (.a(inst[6:0]), .b(7'b1100011), .eq(comparator_8_eq));  // open: gt, lt
  and and_3 (and_3_out, comparator_8_eq, comparator_2_eq, BrLt);
  Comparator #(.width(7)) comparator_9 (.a(inst[6:0]), .b(7'b1100011), .eq(comparator_9_eq));  // open: gt, lt
  and and_4 (and_4_out, comparator_9_eq, comparator_10_eq, ~BrEq);  // AND_Gate
  Comparator #(.width(3)) comparator_10 (.a(inst[14:12]), .b(3'b001), .eq(comparator_10_eq));  // open: gt, lt
  Comparator #(.width(7)) comparator_11 (.a(inst[6:0]), .b(7'b1101111), .eq(comparator_11_eq));  // open: gt, lt
  and and_5 (and_5_out, comparator_1_eq, comparator_3_eq);
  or or_1 (PCSel, and_5_out, and_1_out, and_2_out, and_3_out, and_4_out, comparator_11_eq);
  Comparator #(.width(7)) comparator_12 (.a(inst[6:0]), .b(7'b1100011), .eq(comparator_12_eq));  // open: gt, lt
  ALUSel_0 alusel_0_1 (.in_1(inst), .ALUSel_0(ALUSel[0]));
  ALUSel_1 alusel_1_1 (.in_1(inst), .ALUSel_1(ALUSel[1]));
  ALUSel_2 alusel_2_1 (.in_1(inst), .ALUSel_2(ALUSel[2]));
  ALUSel_3 alusel_3_1 (.in_1(inst), .ALUSel_3(ALUSel[3]));
  Comparator #(.width(3)) comparator_13 (.a(inst[14:12]), .b(3'b110), .eq(comparator_13_eq));  // open: gt, lt
  BSel_0 bsel_0_1 (.in_1(inst), .BSel_0(BSel));
  and and_6 (BrUn, comparator_12_eq, comparator_13_eq);
  Comparator #(.width(7)) comparator_14 (.a(inst[6:0]), .b(7'b1100011), .eq(comparator_14_eq));  // open: gt, lt
  Comparator #(.width(3)) comparator_15 (.a(inst[14:12]), .b(3'b000), .eq(comparator_15_eq));  // open: gt, lt
  Comparator #(.width(7)) comparator_16 (.a(inst[6:0]), .b(7'b1100011), .eq(comparator_16_eq));  // open: gt, lt
  Comparator #(.width(3)) comparator_17 (.a(inst[14:12]), .b(3'b001), .eq(comparator_17_eq));  // open: gt, lt
  Comparator #(.width(32)) comparator_18 (.a(inst), .b({32{1'b0}}), .eq(comparator_18_eq));  // open: gt, lt
  Comparator #(.width(7)) comparator_19 (.a(inst[6:0]), .b(7'b1100011), .eq(comparator_19_eq));  // open: gt, lt
  Comparator #(.width(3)) comparator_20 (.a(inst[14:12]), .b(3'b110), .eq(comparator_20_eq));  // open: gt, lt
  and and_7 (and_7_out, comparator_14_eq, comparator_15_eq);
  Comparator #(.width(7)) comparator_21 (.a(inst[6:0]), .b(7'b0100011), .eq(comparator_21_eq));  // open: gt, lt
  Comparator #(.width(3)) comparator_22 (.a(inst[14:12]), .b(3'b010), .eq(comparator_22_eq));  // open: gt, lt
  Comparator #(.width(7)) comparator_23 (.a(inst[6:0]), .b(7'b1100011), .eq(comparator_23_eq));  // open: gt, lt
  Comparator #(.width(3)) comparator_24 (.a(inst[14:12]), .b(3'b100), .eq(comparator_24_eq));  // open: gt, lt
  and and_8 (and_8_out, comparator_16_eq, comparator_17_eq);
  and and_9 (and_9_out, comparator_19_eq, comparator_20_eq);
  and and_10 (and_10_out, comparator_21_eq, comparator_22_eq);
  and and_11 (and_11_out, comparator_23_eq, comparator_24_eq);
  or or_2 (or_2_out, and_7_out, and_10_out, and_11_out, and_8_out, comparator_18_eq, and_9_out);
  not not_1 (RegWEn, or_2_out);
  Comparator #(.width(3)) comparator_25 (.a(inst[14:12]), .b(3'b010), .eq(comparator_25_eq));  // open: gt, lt
  and and_12 (and_12_out, comparator_25_eq, comparator_26_eq);
  Comparator #(.width(7)) comparator_26 (.a(inst[6:0]), .b(7'b0100011), .eq(comparator_26_eq));  // open: gt, lt
  Comparator #(.width(7)) comparator_27 (.a(inst[6:0]), .b(7'b0110111), .eq(comparator_27_eq));  // open: gt, lt
  Comparator #(.width(7)) comparator_28 (.a(inst[6:0]), .b(7'b1100011), .eq(comparator_28_eq));  // open: gt, lt
  Comparator #(.width(3)) comparator_29 (.a(inst[14:12]), .b(3'b001), .eq(comparator_29_eq));  // open: gt, lt
  Comparator #(.width(7)) comparator_30 (.a(inst[6:0]), .b(7'b1101111), .eq(ImmSel[2]));  // open: gt, lt
  Comparator #(.width(7)) comparator_31 (.a(inst[6:0]), .b(7'b1100011), .eq(comparator_31_eq));  // open: gt, lt
  Comparator #(.width(3)) comparator_32 (.a(inst[14:12]), .b(3'b100), .eq(comparator_32_eq));  // open: gt, lt
  Comparator #(.width(7)) comparator_33 (.a(inst[6:0]), .b(7'b1100011), .eq(comparator_33_eq));  // open: gt, lt
  Comparator #(.width(3)) comparator_34 (.a(inst[14:12]), .b(3'b000), .eq(comparator_34_eq));  // open: gt, lt
  and and_13 (and_13_out, comparator_28_eq, comparator_29_eq);
  Comparator #(.width(7)) comparator_35 (.a(inst[6:0]), .b(7'b1100011), .eq(comparator_35_eq));  // open: gt, lt
  Comparator #(.width(3)) comparator_36 (.a(inst[14:12]), .b(3'b110), .eq(comparator_36_eq));  // open: gt, lt
  Comparator #(.width(7)) comparator_37 (.a(inst[6:0]), .b(7'b0110111), .eq(comparator_37_eq));  // open: gt, lt
  or or_3 (ImmSel[0], and_12_out, comparator_27_eq);
  and and_14 (and_14_out, comparator_31_eq, comparator_32_eq);
  and and_15 (and_15_out, comparator_33_eq, comparator_34_eq);
  and and_16 (and_16_out, comparator_35_eq, comparator_36_eq);
  or or_4 (ImmSel[1], and_14_out, and_15_out, and_13_out, and_16_out, comparator_37_eq);
  Comparator #(.width(7)) comparator_38 (.a(inst[6:0]), .b(7'b0000011), .eq(comparator_38_eq));  // open: gt, lt
  Comparator #(.width(3)) comparator_39 (.a(inst[14:12]), .b(3'b000), .eq(comparator_39_eq));  // open: gt, lt
  Comparator #(.width(7)) comparator_40 (.a(inst[6:0]), .b(7'b0000011), .eq(comparator_40_eq));  // open: gt, lt
  Comparator #(.width(3)) comparator_41 (.a(inst[14:12]), .b(3'b010), .eq(comparator_41_eq));  // open: gt, lt
  Comparator #(.width(7)) comparator_42 (.a(inst[6:0]), .b(7'b1100111), .eq(comparator_42_eq));  // open: gt, lt
  Comparator #(.width(3)) comparator_43 (.a(inst[14:12]), .b(3'b000), .eq(comparator_43_eq));  // open: gt, lt
  and and_17 (and_17_out, comparator_38_eq, comparator_39_eq);
  and and_18 (and_18_out, comparator_40_eq, comparator_41_eq);
  and and_19 (and_19_out, comparator_42_eq, comparator_43_eq);
  Comparator #(.width(7)) comparator_44 (.a(inst[6:0]), .b(7'b1101111), .eq(comparator_44_eq));  // open: gt, lt
  Comparator #(.width(7)) comparator_45 (.a(inst[6:0]), .b(7'b0000011), .eq(comparator_45_eq));  // open: gt, lt
  Comparator #(.width(3)) comparator_46 (.a(inst[14:12]), .b(3'b001), .eq(comparator_46_eq));  // open: gt, lt
  Comparator #(.width(7)) comparator_47 (.a(inst[6:0]), .b(7'b1100011), .eq(comparator_47_eq));  // open: gt, lt
  Comparator #(.width(3)) comparator_48 (.a(inst[14:12]), .b(3'b000), .eq(comparator_48_eq));  // open: gt, lt
  Comparator #(.width(7)) comparator_49 (.a(inst[6:0]), .b(7'b1100011), .eq(comparator_49_eq));  // open: gt, lt
  Comparator #(.width(3)) comparator_50 (.a(inst[14:12]), .b(3'b100), .eq(comparator_50_eq));  // open: gt, lt
  Comparator #(.width(7)) comparator_51 (.a(inst[6:0]), .b(7'b1100011), .eq(comparator_51_eq));  // open: gt, lt
  Comparator #(.width(3)) comparator_52 (.a(inst[14:12]), .b(3'b001), .eq(comparator_52_eq));  // open: gt, lt
  Comparator #(.width(7)) comparator_53 (.a(inst[6:0]), .b(7'b1100011), .eq(comparator_53_eq));  // open: gt, lt
  Comparator #(.width(3)) comparator_54 (.a(inst[14:12]), .b(3'b110), .eq(comparator_54_eq));  // open: gt, lt
  Comparator #(.width(7)) comparator_55 (.a(inst[6:0]), .b(7'b1101111), .eq(comparator_55_eq));  // open: gt, lt
  Comparator #(.width(3)) comparator_56 (.a(inst[14:12]), .b(3'b010), .eq(comparator_56_eq));  // open: gt, lt
  and and_20 (and_20_out, comparator_45_eq, comparator_46_eq);
  and and_21 (and_21_out, comparator_47_eq, comparator_48_eq);
  and and_22 (and_22_out, comparator_49_eq, comparator_50_eq);
  and and_23 (and_23_out, comparator_51_eq, comparator_52_eq);
  and and_24 (and_24_out, comparator_53_eq, comparator_54_eq);
  and and_25 (MemRW, comparator_56_eq, comparator_57_eq);
  Comparator #(.width(7)) comparator_57 (.a(inst[6:0]), .b(7'b0100011), .eq(comparator_57_eq));  // open: gt, lt
  or or_5 (or_5_out, and_17_out, and_18_out, and_19_out, comparator_44_eq, and_20_out);
  not not_2 (WBSel[0], or_5_out);
  or or_6 (ASel, and_21_out, and_22_out, and_23_out, and_24_out, comparator_55_eq);
  Comparator #(.width(7)) comparator_58 (.a(inst[6:0]), .b(7'b0000011), .eq(comparator_58_eq));  // open: gt, lt
  Comparator #(.width(3)) comparator_59 (.a(inst[14:12]), .b(3'b000), .eq(comparator_59_eq));  // open: gt, lt
  Comparator #(.width(7)) comparator_60 (.a(inst[6:0]), .b(7'b0000011), .eq(comparator_60_eq));  // open: gt, lt
  Comparator #(.width(3)) comparator_61 (.a(inst[14:12]), .b(3'b010), .eq(comparator_61_eq));  // open: gt, lt
  Comparator #(.width(7)) comparator_62 (.a(inst[6:0]), .b(7'b0000011), .eq(comparator_62_eq));  // open: gt, lt
  Comparator #(.width(3)) comparator_63 (.a(inst[14:12]), .b(3'b001), .eq(comparator_63_eq));  // open: gt, lt
  and and_26 (and_26_out, comparator_58_eq, comparator_59_eq);
  and and_27 (and_27_out, comparator_60_eq, comparator_61_eq);
  and and_28 (and_28_out, comparator_62_eq, comparator_63_eq);
  or or_7 (WBSel[1], and_26_out, and_27_out, and_28_out);

  // Other names for the same wires on the sheet: opcode[6:0] = inst[6:0]; Funct3[2:0] = inst[14:12];
  //   Funct7[6:0] = inst[31:25]

  // Notes on the sheet:
  //   INPUTS to your circuit
  //   PCSel
  //   DON'T CHANGE THE LOCATIONS OF THE INPUTS AND OUTPUTS!
  //   OUTPUT from your circuit
endmodule

module ALUSel_0 (
  input  [31:0] in_1,
  output ALUSel_0
);

  wire and_1_out, and_2_out, and_3_out, and_4_out, and_5_out, and_6_out, and_7_out, and_8_out, and_9_out,
       and_10_out, comparator_1_eq, comparator_2_eq, comparator_3_eq, comparator_4_eq, comparator_5_eq,
       comparator_6_eq, comparator_7_eq, comparator_8_eq, comparator_9_eq, comparator_10_eq,
       comparator_11_eq, comparator_12_eq, comparator_13_eq, comparator_14_eq, comparator_15_eq,
       comparator_16_eq, comparator_17_eq, comparator_18_eq, comparator_19_eq, comparator_20_eq,
       comparator_21_eq, comparator_22_eq, comparator_23_eq, comparator_24_eq, comparator_25_eq,
       comparator_26_eq, comparator_27_eq, comparator_28_eq;

  Comparator #(.width(7)) comparator_1 (.a(in_1[6:0]), .b(7'b0110011), .eq(comparator_1_eq));  // open: gt, lt
  Comparator #(.width(3)) comparator_2 (.a(in_1[14:12]), .b(3'b010), .eq(comparator_2_eq));  // open: gt, lt
  Comparator #(.width(7)) comparator_3 (.a(in_1[31:25]), .b({7{1'b0}}), .eq(comparator_3_eq));  // open: gt, lt
  Comparator #(.width(7)) comparator_4 (.a(in_1[6:0]), .b(7'b0110011), .eq(comparator_4_eq));  // open: gt, lt
  Comparator #(.width(3)) comparator_5 (.a(in_1[14:12]), .b(3'b101), .eq(comparator_5_eq));  // open: gt, lt
  Comparator #(.width(7)) comparator_6 (.a(in_1[31:25]), .b(7'b0100000), .eq(comparator_6_eq));  // open: gt, lt
  Comparator #(.width(7)) comparator_7 (.a(in_1[6:0]), .b(7'b0110011), .eq(comparator_7_eq));  // open: gt, lt
  and and_1 (and_1_out, comparator_7_eq, comparator_8_eq, comparator_9_eq);
  Comparator #(.width(3)) comparator_8 (.a(in_1[14:12]), .b(3'b011), .eq(comparator_8_eq));  // open: gt, lt
  Comparator #(.width(7)) comparator_9 (.a(in_1[31:25]), .b(7'b0000001), .eq(comparator_9_eq));  // open: gt, lt
  Comparator #(.width(7)) comparator_10 (.a(in_1[6:0]), .b(7'b0110011), .eq(comparator_10_eq));  // open: gt, lt
  Comparator #(.width(3)) comparator_11 (.a(in_1[14:12]), .b(3'b100), .eq(comparator_11_eq));  // open: gt, lt
  Comparator #(.width(7)) comparator_12 (.a(in_1[31:25]), .b({7{1'b0}}), .eq(comparator_12_eq));  // open: gt, lt
  and and_2 (and_2_out, comparator_1_eq, comparator_2_eq, comparator_3_eq);
  and and_3 (and_3_out, comparator_4_eq, comparator_5_eq, comparator_6_eq);
  and and_4 (and_4_out, comparator_10_eq, comparator_11_eq, comparator_12_eq);
  Comparator #(.width(7)) comparator_13 (.a(in_1[6:0]), .b(7'b0110011), .eq(comparator_13_eq));  // open: gt, lt
  Comparator #(.width(3)) comparator_14 (.a(in_1[14:12]), .b(3'b111), .eq(comparator_14_eq));  // open: gt, lt
  Comparator #(.width(7)) comparator_15 (.a(in_1[31:25]), .b(7'b0000001), .eq(comparator_15_eq));  // open: gt, lt
  Comparator #(.width(7)) comparator_16 (.a(in_1[6:0]), .b(7'b0010011), .eq(comparator_16_eq));  // open: gt, lt
  Comparator #(.width(3)) comparator_17 (.a(in_1[14:12]), .b(3'b101), .eq(comparator_17_eq));  // open: gt, lt
  Comparator #(.width(7)) comparator_18 (.a(in_1[31:25]), .b(7'b0100000), .eq(comparator_18_eq));  // open: gt, lt
  Comparator #(.width(7)) comparator_19 (.a(in_1[6:0]), .b(7'b0110111), .eq(comparator_19_eq));  // open: gt, lt
  Comparator #(.width(7)) comparator_20 (.a(in_1[6:0]), .b(7'b0110011), .eq(comparator_20_eq));  // open: gt, lt
  Comparator #(.width(3)) comparator_21 (.a(in_1[14:12]), .b(3'b111), .eq(comparator_21_eq));  // open: gt, lt
  Comparator #(.width(7)) comparator_22 (.a(in_1[31:25]), .b({7{1'b0}}), .eq(comparator_22_eq));  // open: gt, lt
  and and_5 (and_5_out, comparator_13_eq, comparator_14_eq, comparator_15_eq);
  and and_6 (and_6_out, comparator_16_eq, comparator_17_eq, comparator_18_eq);
  and and_7 (and_7_out, comparator_20_eq, comparator_21_eq, comparator_22_eq);
  Comparator #(.width(7)) comparator_23 (.a(in_1[6:0]), .b(7'b0010011), .eq(comparator_23_eq));  // open: gt, lt
  Comparator #(.width(3)) comparator_24 (.a(in_1[14:12]), .b(3'b010), .eq(comparator_24_eq));  // open: gt, lt
  Comparator #(.width(7)) comparator_25 (.a(in_1[6:0]), .b(7'b0010011), .eq(comparator_25_eq));  // open: gt, lt
  Comparator #(.width(3)) comparator_26 (.a(in_1[14:12]), .b(3'b100), .eq(comparator_26_eq));  // open: gt, lt
  Comparator #(.width(7)) comparator_27 (.a(in_1[6:0]), .b(7'b0010011), .eq(comparator_27_eq));  // open: gt, lt
  Comparator #(.width(3)) comparator_28 (.a(in_1[14:12]), .b(3'b111), .eq(comparator_28_eq));  // open: gt, lt
  and and_8 (and_8_out, comparator_23_eq, comparator_24_eq);
  and and_9 (and_9_out, comparator_25_eq, comparator_26_eq);
  and and_10 (and_10_out, comparator_27_eq, comparator_28_eq);
  or or_1 (ALUSel_0, and_7_out, and_5_out, and_2_out, and_10_out, comparator_19_eq, and_3_out, and_1_out, and_4_out, and_6_out, and_8_out, and_9_out);

  // Other names for the same wires on the sheet: inst[31:0] = in_1; opcode[6:0] = in_1[6:0];
  //   Funct3[2:0] = in_1[14:12]; Funct7[6:0] = in_1[31:25]

  // Notes on the sheet:
  //   INPUTS to your circuit
endmodule

module ALUSel_1 (
  input  [31:0] in_1,
  output ALUSel_1
);

  wire and_1_out, and_2_out, and_3_out, and_4_out, and_5_out, and_6_out, and_7_out, and_8_out, and_9_out,
       and_10_out, and_11_out, comparator_1_eq, comparator_2_eq, comparator_3_eq, comparator_4_eq,
       comparator_5_eq, comparator_6_eq, comparator_7_eq, comparator_8_eq, comparator_9_eq, comparator_10_eq,
       comparator_11_eq, comparator_12_eq, comparator_13_eq, comparator_14_eq, comparator_15_eq,
       comparator_16_eq, comparator_17_eq, comparator_18_eq, comparator_19_eq, comparator_20_eq,
       comparator_21_eq, comparator_22_eq, comparator_23_eq, comparator_24_eq, comparator_25_eq,
       comparator_26_eq, comparator_27_eq, comparator_28_eq, comparator_29_eq, comparator_30_eq;

  Comparator #(.width(7)) comparator_1 (.a(in_1[6:0]), .b(7'b0110011), .eq(comparator_1_eq));  // open: gt, lt
  Comparator #(.width(3)) comparator_2 (.a(in_1[14:12]), .b(3'b000), .eq(comparator_2_eq));  // open: gt, lt
  Comparator #(.width(7)) comparator_3 (.a(in_1[31:25]), .b(7'b0000001), .eq(comparator_3_eq));  // open: gt, lt
  Comparator #(.width(7)) comparator_4 (.a(in_1[6:0]), .b(7'b0110011), .eq(comparator_4_eq));  // open: gt, lt
  Comparator #(.width(3)) comparator_5 (.a(in_1[14:12]), .b(3'b001), .eq(comparator_5_eq));  // open: gt, lt
  Comparator #(.width(7)) comparator_6 (.a(in_1[31:25]), .b({7{1'b0}}), .eq(comparator_6_eq));  // open: gt, lt
  Comparator #(.width(7)) comparator_7 (.a(in_1[6:0]), .b(7'b0110011), .eq(comparator_7_eq));  // open: gt, lt
  Comparator #(.width(3)) comparator_8 (.a(in_1[14:12]), .b(3'b001), .eq(comparator_8_eq));  // open: gt, lt
  and and_1 (and_1_out, comparator_7_eq, comparator_8_eq, comparator_9_eq);
  Comparator #(.width(7)) comparator_9 (.a(in_1[31:25]), .b(7'b0000001), .eq(comparator_9_eq));  // open: gt, lt
  Comparator #(.width(7)) comparator_10 (.a(in_1[6:0]), .b(7'b0110011), .eq(comparator_10_eq));  // open: gt, lt
  and and_2 (and_2_out, comparator_10_eq, comparator_11_eq, comparator_12_eq);
  Comparator #(.width(3)) comparator_11 (.a(in_1[14:12]), .b(3'b010), .eq(comparator_11_eq));  // open: gt, lt
  Comparator #(.width(7)) comparator_12 (.a(in_1[31:25]), .b({7{1'b0}}), .eq(comparator_12_eq));  // open: gt, lt
  and and_3 (and_3_out, comparator_1_eq, comparator_2_eq, comparator_3_eq);
  and and_4 (and_4_out, comparator_4_eq, comparator_5_eq, comparator_6_eq);
  Comparator #(.width(7)) comparator_13 (.a(in_1[6:0]), .b(7'b0010011), .eq(comparator_13_eq));  // open: gt, lt
  Comparator #(.width(3)) comparator_14 (.a(in_1[14:12]), .b(3'b001), .eq(comparator_14_eq));  // open: gt, lt
  Comparator #(.width(7)) comparator_15 (.a(in_1[31:25]), .b({7{1'b0}}), .eq(comparator_15_eq));  // open: gt, lt
  Comparator #(.width(7)) comparator_16 (.a(in_1[6:0]), .b(7'b0110011), .eq(comparator_16_eq));  // open: gt, lt
  Comparator #(.width(3)) comparator_17 (.a(in_1[14:12]), .b(3'b100), .eq(comparator_17_eq));  // open: gt, lt
  Comparator #(.width(7)) comparator_18 (.a(in_1[31:25]), .b({7{1'b0}}), .eq(comparator_18_eq));  // open: gt, lt
  Comparator #(.width(7)) comparator_19 (.a(in_1[6:0]), .b(7'b0110011), .eq(comparator_19_eq));  // open: gt, lt
  and and_5 (and_5_out, comparator_19_eq, comparator_20_eq, comparator_21_eq);
  Comparator #(.width(3)) comparator_20 (.a(in_1[14:12]), .b(3'b110), .eq(comparator_20_eq));  // open: gt, lt
  Comparator #(.width(7)) comparator_21 (.a(in_1[31:25]), .b({7{1'b0}}), .eq(comparator_21_eq));  // open: gt, lt
  and and_6 (and_6_out, comparator_13_eq, comparator_14_eq, comparator_15_eq);
  Comparator #(.width(7)) comparator_22 (.a(in_1[6:0]), .b(7'b0110011), .eq(comparator_22_eq));  // open: gt, lt
  Comparator #(.width(3)) comparator_23 (.a(in_1[14:12]), .b(3'b011), .eq(comparator_23_eq));  // open: gt, lt
  Comparator #(.width(7)) comparator_24 (.a(in_1[31:25]), .b(7'b0000001), .eq(comparator_24_eq));  // open: gt, lt
  and and_7 (and_7_out, comparator_16_eq, comparator_17_eq, comparator_18_eq);
  and and_8 (and_8_out, comparator_22_eq, comparator_23_eq, comparator_24_eq);
  Comparator #(.width(7)) comparator_25 (.a(in_1[6:0]), .b(7'b0010011), .eq(comparator_25_eq));  // open: gt, lt
  Comparator #(.width(3)) comparator_26 (.a(in_1[14:12]), .b(3'b010), .eq(comparator_26_eq));  // open: gt, lt
  Comparator #(.width(7)) comparator_27 (.a(in_1[6:0]), .b(7'b0010011), .eq(comparator_27_eq));  // open: gt, lt
  and and_9 (and_9_out, comparator_27_eq, comparator_28_eq);
  Comparator #(.width(3)) comparator_28 (.a(in_1[14:12]), .b(3'b100), .eq(comparator_28_eq));  // open: gt, lt
  Comparator #(.width(7)) comparator_29 (.a(in_1[6:0]), .b(7'b0010011), .eq(comparator_29_eq));  // open: gt, lt
  Comparator #(.width(3)) comparator_30 (.a(in_1[14:12]), .b(3'b110), .eq(comparator_30_eq));  // open: gt, lt
  and and_10 (and_10_out, comparator_25_eq, comparator_26_eq);
  and and_11 (and_11_out, comparator_29_eq, comparator_30_eq);
  or or_1 (ALUSel_1, and_8_out, and_7_out, and_3_out, and_11_out, and_6_out, and_4_out, and_1_out, and_2_out, and_5_out, and_10_out, and_9_out);

  // Other names for the same wires on the sheet: inst[31:0] = in_1; opcode[6:0] = in_1[6:0];
  //   Funct3[2:0] = in_1[14:12]; Funct7[6:0] = in_1[31:25]

  // Notes on the sheet:
  //   INPUTS to your circuit
endmodule

module ALUSel_2 (
  input  [31:0] in_1,
  output ALUSel_2
);

  wire and_1_out, and_2_out, and_3_out, and_4_out, and_5_out, and_6_out, and_7_out, and_8_out, and_9_out,
       and_10_out, comparator_1_eq, comparator_2_eq, comparator_3_eq, comparator_4_eq, comparator_5_eq,
       comparator_6_eq, comparator_7_eq, comparator_8_eq, comparator_9_eq, comparator_10_eq,
       comparator_11_eq, comparator_12_eq, comparator_13_eq, comparator_14_eq, comparator_15_eq,
       comparator_16_eq, comparator_17_eq, comparator_18_eq, comparator_19_eq, comparator_20_eq,
       comparator_21_eq, comparator_22_eq, comparator_23_eq, comparator_24_eq, comparator_25_eq,
       comparator_26_eq, comparator_27_eq, comparator_28_eq, comparator_29_eq, comparator_30_eq;

  Comparator #(.width(7)) comparator_1 (.a(in_1[6:0]), .b(7'b0110011), .eq(comparator_1_eq));  // open: gt, lt
  Comparator #(.width(3)) comparator_2 (.a(in_1[14:12]), .b(3'b000), .eq(comparator_2_eq));  // open: gt, lt
  Comparator #(.width(7)) comparator_3 (.a(in_1[31:25]), .b(7'b0100000), .eq(comparator_3_eq));  // open: gt, lt
  Comparator #(.width(7)) comparator_4 (.a(in_1[6:0]), .b(7'b0110011), .eq(comparator_4_eq));  // open: gt, lt
  Comparator #(.width(3)) comparator_5 (.a(in_1[14:12]), .b(3'b001), .eq(comparator_5_eq));  // open: gt, lt
  Comparator #(.width(7)) comparator_6 (.a(in_1[31:25]), .b(7'b0000001), .eq(comparator_6_eq));  // open: gt, lt
  Comparator #(.width(7)) comparator_7 (.a(in_1[6:0]), .b(7'b0110011), .eq(comparator_7_eq));  // open: gt, lt
  and and_1 (and_1_out, comparator_7_eq, comparator_8_eq, comparator_9_eq);
  Comparator #(.width(3)) comparator_8 (.a(in_1[14:12]), .b(3'b001), .eq(comparator_8_eq));  // open: gt, lt
  Comparator #(.width(7)) comparator_9 (.a(in_1[31:25]), .b({7{1'b0}}), .eq(comparator_9_eq));  // open: gt, lt
  Comparator #(.width(7)) comparator_10 (.a(in_1[6:0]), .b(7'b0110011), .eq(comparator_10_eq));  // open: gt, lt
  Comparator #(.width(3)) comparator_11 (.a(in_1[14:12]), .b(3'b101), .eq(comparator_11_eq));  // open: gt, lt
  and and_2 (and_2_out, comparator_10_eq, comparator_11_eq, comparator_12_eq);
  Comparator #(.width(7)) comparator_12 (.a(in_1[31:25]), .b({7{1'b0}}), .eq(comparator_12_eq));  // open: gt, lt
  and and_3 (and_3_out, comparator_1_eq, comparator_2_eq, comparator_3_eq);
  and and_4 (and_4_out, comparator_4_eq, comparator_5_eq, comparator_6_eq);
  Comparator #(.width(7)) comparator_13 (.a(in_1[6:0]), .b(7'b0010011), .eq(comparator_13_eq));  // open: gt, lt
  Comparator #(.width(3)) comparator_14 (.a(in_1[14:12]), .b(3'b101), .eq(comparator_14_eq));  // open: gt, lt
  Comparator #(.width(7)) comparator_15 (.a(in_1[31:25]), .b(7'b0100000), .eq(comparator_15_eq));  // open: gt, lt
  Comparator #(.width(7)) comparator_16 (.a(in_1[6:0]), .b(7'b0110011), .eq(comparator_16_eq));  // open: gt, lt
  Comparator #(.width(3)) comparator_17 (.a(in_1[14:12]), .b(3'b101), .eq(comparator_17_eq));  // open: gt, lt
  Comparator #(.width(7)) comparator_18 (.a(in_1[31:25]), .b(7'b0100000), .eq(comparator_18_eq));  // open: gt, lt
  Comparator #(.width(7)) comparator_19 (.a(in_1[6:0]), .b(7'b0110011), .eq(comparator_19_eq));  // open: gt, lt
  and and_5 (and_5_out, comparator_19_eq, comparator_20_eq, comparator_21_eq);
  Comparator #(.width(3)) comparator_20 (.a(in_1[14:12]), .b(3'b010), .eq(comparator_20_eq));  // open: gt, lt
  Comparator #(.width(7)) comparator_21 (.a(in_1[31:25]), .b({7{1'b0}}), .eq(comparator_21_eq));  // open: gt, lt
  and and_6 (and_6_out, comparator_13_eq, comparator_14_eq, comparator_15_eq);
  Comparator #(.width(7)) comparator_22 (.a(in_1[6:0]), .b(7'b0010011), .eq(comparator_22_eq));  // open: gt, lt
  Comparator #(.width(3)) comparator_23 (.a(in_1[14:12]), .b(3'b001), .eq(comparator_23_eq));  // open: gt, lt
  Comparator #(.width(7)) comparator_24 (.a(in_1[31:25]), .b({7{1'b0}}), .eq(comparator_24_eq));  // open: gt, lt
  and and_7 (and_7_out, comparator_16_eq, comparator_17_eq, comparator_18_eq);
  and and_8 (and_8_out, comparator_22_eq, comparator_23_eq, comparator_24_eq);
  Comparator #(.width(7)) comparator_25 (.a(in_1[6:0]), .b(7'b0010011), .eq(comparator_25_eq));  // open: gt, lt
  Comparator #(.width(3)) comparator_26 (.a(in_1[14:12]), .b(3'b010), .eq(comparator_26_eq));  // open: gt, lt
  Comparator #(.width(7)) comparator_27 (.a(in_1[6:0]), .b(7'b0010011), .eq(comparator_27_eq));  // open: gt, lt
  and and_9 (and_9_out, comparator_27_eq, comparator_28_eq, comparator_29_eq);
  Comparator #(.width(3)) comparator_28 (.a(in_1[14:12]), .b(3'b101), .eq(comparator_28_eq));  // open: gt, lt
  Comparator #(.width(7)) comparator_29 (.a(in_1[31:25]), .b({7{1'b0}}), .eq(comparator_29_eq));  // open: gt, lt
  and and_10 (and_10_out, comparator_25_eq, comparator_26_eq);
  Comparator #(.width(7)) comparator_30 (.a(in_1[6:0]), .b(7'b0110111), .eq(comparator_30_eq));  // open: gt, lt
  or or_1 (ALUSel_2, and_8_out, and_7_out, and_3_out, comparator_30_eq, and_6_out, and_4_out, and_1_out, and_2_out, and_5_out, and_10_out, and_9_out);

  // Other names for the same wires on the sheet: inst[31:0] = in_1; opcode[6:0] = in_1[6:0];
  //   Funct3[2:0] = in_1[14:12]; Funct7[6:0] = in_1[31:25]

  // Notes on the sheet:
  //   INPUTS to your circuit
endmodule

module ALUSel_3 (
  input  [31:0] in_1,
  output ALUSel_3
);

  wire and_1_out, and_2_out, and_3_out, and_4_out, and_5_out, and_6_out, comparator_1_eq, comparator_2_eq,
       comparator_3_eq, comparator_4_eq, comparator_5_eq, comparator_6_eq, comparator_7_eq, comparator_8_eq,
       comparator_9_eq, comparator_10_eq, comparator_11_eq, comparator_12_eq, comparator_13_eq,
       comparator_14_eq, comparator_15_eq, comparator_16_eq, comparator_17_eq, comparator_18_eq,
       comparator_19_eq;

  Comparator #(.width(7)) comparator_1 (.a(in_1[6:0]), .b(7'b0110011), .eq(comparator_1_eq));  // open: gt, lt
  Comparator #(.width(3)) comparator_2 (.a(in_1[14:12]), .b(3'b000), .eq(comparator_2_eq));  // open: gt, lt
  Comparator #(.width(7)) comparator_3 (.a(in_1[31:25]), .b(7'b0000001), .eq(comparator_3_eq));  // open: gt, lt
  Comparator #(.width(7)) comparator_4 (.a(in_1[6:0]), .b(7'b0110011), .eq(comparator_4_eq));  // open: gt, lt
  Comparator #(.width(3)) comparator_5 (.a(in_1[14:12]), .b(3'b011), .eq(comparator_5_eq));  // open: gt, lt
  Comparator #(.width(7)) comparator_6 (.a(in_1[31:25]), .b(7'b0000001), .eq(comparator_6_eq));  // open: gt, lt
  Comparator #(.width(7)) comparator_7 (.a(in_1[6:0]), .b(7'b0110111), .eq(comparator_7_eq));  // open: gt, lt
  and and_1 (and_1_out, comparator_1_eq, comparator_2_eq, comparator_3_eq);
  and and_2 (and_2_out, comparator_4_eq, comparator_5_eq, comparator_6_eq);
  Comparator #(.width(7)) comparator_8 (.a(in_1[6:0]), .b(7'b0110011), .eq(comparator_8_eq));  // open: gt, lt
  Comparator #(.width(3)) comparator_9 (.a(in_1[14:12]), .b(3'b000), .eq(comparator_9_eq));  // open: gt, lt
  Comparator #(.width(7)) comparator_10 (.a(in_1[31:25]), .b(7'b0100000), .eq(comparator_10_eq));  // open: gt, lt
  and and_3 (and_3_out, comparator_8_eq, comparator_9_eq, comparator_10_eq);
  Comparator #(.width(7)) comparator_11 (.a(in_1[6:0]), .b(7'b0110011), .eq(comparator_11_eq));  // open: gt, lt
  Comparator #(.width(3)) comparator_12 (.a(in_1[14:12]), .b(3'b101), .eq(comparator_12_eq));  // open: gt, lt
  Comparator #(.width(7)) comparator_13 (.a(in_1[31:25]), .b(7'b0000001), .eq(comparator_13_eq));  // open: gt, lt
  and and_4 (and_4_out, comparator_11_eq, comparator_12_eq, comparator_13_eq);
  or or_1 (ALUSel_3, and_1_out, and_2_out, comparator_7_eq, and_3_out, and_4_out, and_6_out, and_5_out);
  Comparator #(.width(3)) comparator_14 (.a(in_1[14:12]), .b(3'b001), .eq(comparator_14_eq));  // open: gt, lt
  Comparator #(.width(7)) comparator_15 (.a(in_1[31:25]), .b(7'b0000001), .eq(comparator_15_eq));  // open: gt, lt
  Comparator #(.width(7)) comparator_16 (.a(in_1[6:0]), .b(7'b0110011), .eq(comparator_16_eq));  // open: gt, lt
  Comparator #(.width(7)) comparator_17 (.a(in_1[6:0]), .b(7'b0110011), .eq(comparator_17_eq));  // open: gt, lt
  Comparator #(.width(3)) comparator_18 (.a(in_1[14:12]), .b(3'b111), .eq(comparator_18_eq));  // open: gt, lt
  Comparator #(.width(7)) comparator_19 (.a(in_1[31:25]), .b(7'b0000001), .eq(comparator_19_eq));  // open: gt, lt
  and and_5 (and_5_out, comparator_16_eq, comparator_14_eq, comparator_15_eq);
  and and_6 (and_6_out, comparator_17_eq, comparator_18_eq, comparator_19_eq);

  // Other names for the same wires on the sheet: inst[31:0] = in_1; opcode[6:0] = in_1[6:0];
  //   Funct3[2:0] = in_1[14:12]; Funct7[6:0] = in_1[31:25]

  // Notes on the sheet:
  //   INPUTS to your circuit
endmodule

module BSel_0 (
  input  [31:0] in_1,
  output BSel_0
);

  wire and_1_out, and_2_out, and_3_out, and_4_out, and_5_out, and_6_out, and_7_out, and_8_out, and_9_out,
       and_10_out, and_11_out, and_12_out, and_13_out, and_14_out, comparator_1_eq, comparator_2_eq,
       comparator_3_eq, comparator_4_eq, comparator_5_eq, comparator_6_eq, comparator_7_eq, comparator_8_eq,
       comparator_9_eq, comparator_10_eq, comparator_11_eq, comparator_12_eq, comparator_13_eq,
       comparator_14_eq, comparator_15_eq, comparator_16_eq, comparator_17_eq, comparator_18_eq,
       comparator_19_eq, comparator_20_eq, comparator_21_eq, comparator_22_eq, comparator_23_eq,
       comparator_24_eq, comparator_25_eq, comparator_26_eq, comparator_27_eq, comparator_28_eq,
       comparator_29_eq, comparator_30_eq, comparator_31_eq, comparator_32_eq, comparator_33_eq,
       comparator_34_eq, comparator_35_eq, comparator_36_eq, comparator_37_eq, comparator_38_eq,
       comparator_39_eq, comparator_40_eq, comparator_41_eq, comparator_42_eq, or_1_out;

  Comparator #(.width(7)) comparator_1 (.a(in_1[6:0]), .b(7'b0110011), .eq(comparator_1_eq));  // open: gt, lt
  Comparator #(.width(3)) comparator_2 (.a(in_1[14:12]), .b(3'b011), .eq(comparator_2_eq));  // open: gt, lt
  Comparator #(.width(7)) comparator_3 (.a(in_1[31:25]), .b(7'b0000001), .eq(comparator_3_eq));  // open: gt, lt
  Comparator #(.width(7)) comparator_4 (.a(in_1[6:0]), .b(7'b0110011), .eq(comparator_4_eq));  // open: gt, lt
  Comparator #(.width(3)) comparator_5 (.a(in_1[14:12]), .b(3'b111), .eq(comparator_5_eq));  // open: gt, lt
  Comparator #(.width(7)) comparator_6 (.a(in_1[31:25]), .b({7{1'b0}}), .eq(comparator_6_eq));  // open: gt, lt
  Comparator #(.width(7)) comparator_7 (.a(in_1[6:0]), .b(7'b0110011), .eq(comparator_7_eq));  // open: gt, lt
  Comparator #(.width(3)) comparator_8 (.a(in_1[14:12]), .b(3'b101), .eq(comparator_8_eq));  // open: gt, lt
  and and_1 (and_1_out, comparator_7_eq, comparator_8_eq, comparator_9_eq);
  Comparator #(.width(7)) comparator_9 (.a(in_1[31:25]), .b({7{1'b0}}), .eq(comparator_9_eq));  // open: gt, lt
  Comparator #(.width(7)) comparator_10 (.a(in_1[6:0]), .b(7'b0110011), .eq(comparator_10_eq));  // open: gt, lt
  Comparator #(.width(3)) comparator_11 (.a(in_1[14:12]), .b(3'b111), .eq(comparator_11_eq));  // open: gt, lt
  Comparator #(.width(7)) comparator_12 (.a(in_1[31:25]), .b(7'b0000001), .eq(comparator_12_eq));  // open: gt, lt
  and and_2 (and_2_out, comparator_1_eq, comparator_2_eq, comparator_3_eq);
  and and_3 (and_3_out, comparator_4_eq, comparator_5_eq, comparator_6_eq);
  and and_4 (and_4_out, comparator_10_eq, comparator_11_eq, comparator_12_eq);
  Comparator #(.width(7)) comparator_13 (.a(in_1[6:0]), .b(7'b0110011), .eq(comparator_13_eq));  // open: gt, lt
  Comparator #(.width(3)) comparator_14 (.a(in_1[14:12]), .b(3'b001), .eq(comparator_14_eq));  // open: gt, lt
  Comparator #(.width(7)) comparator_15 (.a(in_1[31:25]), .b(7'b0000001), .eq(comparator_15_eq));  // open: gt, lt
  Comparator #(.width(7)) comparator_16 (.a(in_1[6:0]), .b(7'b0110011), .eq(comparator_16_eq));  // open: gt, lt
  Comparator #(.width(3)) comparator_17 (.a(in_1[14:12]), .b(3'b110), .eq(comparator_17_eq));  // open: gt, lt
  Comparator #(.width(7)) comparator_18 (.a(in_1[31:25]), .b({7{1'b0}}), .eq(comparator_18_eq));  // open: gt, lt
  Comparator #(.width(7)) comparator_19 (.a(in_1[6:0]), .b(7'b0110011), .eq(comparator_19_eq));  // open: gt, lt
  Comparator #(.width(3)) comparator_20 (.a(in_1[14:12]), .b(3'b101), .eq(comparator_20_eq));  // open: gt, lt
  Comparator #(.width(7)) comparator_21 (.a(in_1[31:25]), .b(7'b0000001), .eq(comparator_21_eq));  // open: gt, lt
  and and_5 (and_5_out, comparator_13_eq, comparator_14_eq, comparator_15_eq);
  Comparator #(.width(7)) comparator_22 (.a(in_1[6:0]), .b(7'b0110011), .eq(comparator_22_eq));  // open: gt, lt
  Comparator #(.width(3)) comparator_23 (.a(in_1[14:12]), .b(3'b101), .eq(comparator_23_eq));  // open: gt, lt
  Comparator #(.width(7)) comparator_24 (.a(in_1[31:25]), .b(7'b0100000), .eq(comparator_24_eq));  // open: gt, lt
  and and_6 (and_6_out, comparator_16_eq, comparator_17_eq, comparator_18_eq);
  and and_7 (and_7_out, comparator_19_eq, comparator_20_eq, comparator_21_eq);
  and and_8 (and_8_out, comparator_22_eq, comparator_23_eq, comparator_24_eq);
  Comparator #(.width(7)) comparator_25 (.a(in_1[6:0]), .b(7'b0110011), .eq(comparator_25_eq));  // open: gt, lt
  Comparator #(.width(3)) comparator_26 (.a(in_1[14:12]), .b(3'b000), .eq(comparator_26_eq));  // open: gt, lt
  Comparator #(.width(7)) comparator_27 (.a(in_1[31:25]), .b(7'b0100000), .eq(comparator_27_eq));  // open: gt, lt
  Comparator #(.width(7)) comparator_28 (.a(in_1[6:0]), .b(7'b0110011), .eq(comparator_28_eq));  // open: gt, lt
  Comparator #(.width(3)) comparator_29 (.a(in_1[14:12]), .b(3'b100), .eq(comparator_29_eq));  // open: gt, lt
  Comparator #(.width(7)) comparator_30 (.a(in_1[31:25]), .b({7{1'b0}}), .eq(comparator_30_eq));  // open: gt, lt
  Comparator #(.width(7)) comparator_31 (.a(in_1[6:0]), .b(7'b0110011), .eq(comparator_31_eq));  // open: gt, lt
  Comparator #(.width(3)) comparator_32 (.a(in_1[14:12]), .b(3'b000), .eq(comparator_32_eq));  // open: gt, lt
  Comparator #(.width(7)) comparator_33 (.a(in_1[31:25]), .b(7'b0000001), .eq(comparator_33_eq));  // open: gt, lt
  and and_9 (and_9_out, comparator_25_eq, comparator_26_eq, comparator_27_eq);
  and and_10 (and_10_out, comparator_28_eq, comparator_29_eq, comparator_30_eq);
  and and_11 (and_11_out, comparator_31_eq, comparator_32_eq, comparator_33_eq);
  Comparator #(.width(7)) comparator_34 (.a(in_1[6:0]), .b(7'b0110011), .eq(comparator_34_eq));  // open: gt, lt
  Comparator #(.width(3)) comparator_35 (.a(in_1[14:12]), .b(3'b001), .eq(comparator_35_eq));  // open: gt, lt
  Comparator #(.width(7)) comparator_36 (.a(in_1[31:25]), .b({7{1'b0}}), .eq(comparator_36_eq));  // open: gt, lt
  or or_1 (or_1_out, and_8_out, and_6_out, and_2_out, and_11_out, and_5_out, and_3_out, and_1_out, and_4_out, and_7_out, and_9_out, and_10_out, and_12_out, and_14_out, and_13_out);
  and and_12 (and_12_out, comparator_34_eq, comparator_35_eq, comparator_36_eq);
  Comparator #(.width(7)) comparator_37 (.a(in_1[6:0]), .b(7'b0110011), .eq(comparator_37_eq));  // open: gt, lt
  Comparator #(.width(3)) comparator_38 (.a(in_1[14:12]), .b(3'b010), .eq(comparator_38_eq));  // open: gt, lt
  Comparator #(.width(7)) comparator_39 (.a(in_1[31:25]), .b({7{1'b0}}), .eq(comparator_39_eq));  // open: gt, lt
  not not_1 (BSel_0, or_1_out);
  Comparator #(.width(7)) comparator_40 (.a(in_1[6:0]), .b(7'b0110011), .eq(comparator_40_eq));  // open: gt, lt
  Comparator #(.width(3)) comparator_41 (.a(in_1[14:12]), .b(3'b000), .eq(comparator_41_eq));  // open: gt, lt
  Comparator #(.width(7)) comparator_42 (.a(in_1[31:25]), .b({7{1'b0}}), .eq(comparator_42_eq));  // open: gt, lt
  and and_13 (and_13_out, comparator_37_eq, comparator_38_eq, comparator_39_eq);
  and and_14 (and_14_out, comparator_40_eq, comparator_41_eq, comparator_42_eq);

  // Other names for the same wires on the sheet: inst[31:0] = in_1; opcode[6:0] = in_1[6:0];
  //   Funct3[2:0] = in_1[14:12]; Funct7[6:0] = in_1[31:25]

  // Notes on the sheet:
  //   INPUTS to your circuit
endmodule
