// Logisim project cpu.circ as structural Verilog: 1 circuit, main circuit main
module main (
  input  [31:0] INSTRUCTION,
  input  CLOCK,
  output [31:0] PROGRAM_COUNTER,
  output [31:0] ra,
  output [31:0] sp,
  output [31:0] t0,
  output [31:0] t1,
  output [31:0] t2,
  output [31:0] s0,
  output [31:0] s1,
  output [31:0] a0
);

  wire ASel, BrEq, BrLt, BrUn, BSel, comparator_1_eq, comparator_2_eq, comparator_3_eq, comparator_4_eq,
       MemRW, PCSel, RegWEn;
  wire [1:0] and_1_out, Offset, WBSel;
  wire [2:0] Funct3, immSel;
  wire [3:0] ALUSel;
  wire [6:0] Funct7;
  wire [7:0] multiplexer_5_out;
  wire [15:0] multiplexer_6_out;
  wire [24:0] InstCode;
  wire [31:0] adder_1_out, ALU_Result, bit_extender_1_out, bit_extender_2_out, imm, multiplexer_1_out,
       multiplexer_2_out, multiplexer_3_out, multiplexer_4_out, multiplexer_7_out, PC_Add_4, rData, rs1_Out,
       rs2_Out, thisPC, wb;
  wire [31:2] divider_1_rem;

  Adder #(.width(32)) adder_1 (.a(PROGRAM_COUNTER), .b(32'h4), .out(adder_1_out));  // open: cin, cout
  Multiplexer #(.width(32), .enable("false")) multiplexer_1 (
    .in0(adder_1_out), .in1(ALU_Result), .out(multiplexer_1_out), .sel(PCSel));
  Register #(.width(32)) register_1 (.D(multiplexer_1_out), .clk(CLOCK), .Q(PROGRAM_COUNTER));  // open: en, clr
  Multiplexer #(.width(32), .enable("false")) multiplexer_2 (
    .in0(INSTRUCTION), .in1(32'h13), .out(multiplexer_2_out), .sel(PCSel));
  Register #(.width(32)) register_2 (.D(PROGRAM_COUNTER), .clk(CLOCK), .Q(thisPC));  // open: en, clr
  control_logic control_logic_1 (
    .BSel(BSel), .RegWEn(RegWEn), .ASel(ASel), .ImmSel(immSel), .BrUn(BrUn), .PCSel(PCSel), .BrLt(BrLt),
    .BrEq(BrEq), .inst({Funct7, InstCode[24:15], Funct3, InstCode[11:0]}), .ALUSel(ALUSel), .MemRW(MemRW),
    .WBSel(WBSel));
  Register #(.width(32)) register_3 (
    .D(multiplexer_2_out), .clk(CLOCK), .Q({Funct7, InstCode[24:15], Funct3, InstCode[11:0]}));  // open: en, clr
  Adder #(.width(32)) adder_2 (.a(thisPC), .b(32'h4), .out(PC_Add_4));  // open: cin, cout
  imm_gen imm_gen_1 (.ImmSel(immSel), .imm(imm), .inst({Funct7, InstCode[24:15], Funct3, InstCode[11:0]}));
  regfile_main main_1 (
    .rs2(InstCode[24:20]), .rd(InstCode[11:7]), .Read_Data_1(rs1_Out), .Read_Data_2(rs2_Out), .ra(ra),
    .sp(sp), .t0(t0), .t1(t1), .t2(t2), .s0(s0), .s1(s1), .a0(a0), .rs1(InstCode[19:15]), .Write_Data(wb),
    .RegWEn(RegWEn), .clk(CLOCK));
  branch_comp branch_comp_1 (.BrEq(BrEq), .rs1(rs1_Out), .rs2(rs2_Out), .BrLt(BrLt), .BrUn(BrUn));
  Multiplexer #(.width(32), .enable("false")) multiplexer_3 (
    .in0(rs1_Out), .in1(thisPC), .out(multiplexer_3_out), .sel(ASel));
  Multiplexer #(.width(32), .enable("false")) multiplexer_4 (
    .in0(rs2_Out), .in1(imm), .out(multiplexer_4_out), .sel(BSel));
  alu alu_1 (.Result(ALU_Result), .ALUSel(ALUSel), .A(multiplexer_3_out), .B(multiplexer_4_out));
  Divider #(.width(32)) divider_1 (.a(ALU_Result), .b(32'h4), .rem({divider_1_rem, Offset}));  // open: out, upper
  Multiplexer #(.select(2), .width(8), .enable("false")) multiplexer_5 (
    .in0(rData[7:0]), .in1(rData[15:8]), .in2(rData[23:16]), .in3(rData[31:24]), .out(multiplexer_5_out),
    .sel(Offset));
  Multiplexer #(.select(2), .width(16), .enable("false")) multiplexer_6 (
    .in0(rData[15:0]), .in2(rData[31:16]), .out(multiplexer_6_out), .sel(Offset));  // open: in1, in3
  assign bit_extender_1_out = {{24{multiplexer_5_out[7]}}, multiplexer_5_out};  // Bit_Extender bit_extender_1
  assign bit_extender_2_out = {{16{multiplexer_6_out[15]}}, multiplexer_6_out};  // Bit_Extender bit_extender_2
  // mem_main main_2: pin names not known; wires that end beside it: ALU_Result, rs2_Out, CLOCK, MemRW, rData
  Comparator #(.width(7)) comparator_1 (.a(InstCode[6:0]), .b(7'b0000011), .eq(comparator_1_eq));  // open: gt, lt
  Comparator #(.width(3)) comparator_2 (.a(Funct3), .b(3'b001), .eq(comparator_2_eq));  // open: gt, lt
  Comparator #(.width(7)) comparator_3 (.a(InstCode[6:0]), .b(7'b0000011), .eq(comparator_3_eq));  // open: gt, lt
  Comparator #(.width(3)) comparator_4 (.a(Funct3), .b(3'b010), .eq(comparator_4_eq));  // open: gt, lt
  Multiplexer #(.select(2), .width(32), .enable("false")) multiplexer_7 (
    .in0(bit_extender_1_out), .in1(bit_extender_2_out), .in2(rData), .out(multiplexer_7_out), .sel(and_1_out));  // open: in3
  and and_1 (and_1_out[0], comparator_1_eq, comparator_2_eq);
  and and_2 (and_1_out[1], comparator_3_eq, comparator_4_eq);
  Multiplexer #(.select(2), .width(32), .enable("false")) multiplexer_8 (
    .in0(PC_Add_4), .in1(ALU_Result), .in2(multiplexer_7_out), .out(wb), .sel(WBSel));  // open: in3

  // Other names for the same wires on the sheet: clk = CLOCK; opcode[6:0] = InstCode[6:0]; rd[4:0] = InstCode[11:7];
  //   InstCode (some bits) = {Funct7, Funct3}; rs1[4:0] = InstCode[19:15]; rs2[4:0] = InstCode[24:20]

  // Notes on the sheet:
  //   Output
  //   IMEM (do **NOT** move this)
  //   2-Stages pipelining
  //   Inputs
  //   Instruction Fetch
  //   Instruction Decode
  //   Inputs/Outputs for testing. Do **NOT** move these.
  //   Execute
  //   Memory
endmodule
